# Fritzing sketch LASER GUN UNIT (saved by Fritzing 0.9.5d)
breadboards: 1

parts:
  MCU = Arduino Nano (Rev3.0)
  Reset = Round Pushbutton
  LASER_Fire = Round Pushbutton
  Buzzer = Piezo Speaker
  LASER_Diode = KY-008 Laser Transmitter Module [package="Breakout board"]
  RED_LED = LED - 5mm [color="Red (633nm)" package="5 mm [THT]"]
  R1 = Resistor [tolerance=±5% resistance=220 package="2010 [SMD]"]
  TM1637 = TM1637
  Wireless_Communication = NRF24L01+ Breakout Board
  9V_Battery_(High_Current) = BC9VPC [package=bc9vpc]

nets:
  N1: MCU.D2, TM1637.DIO
  N2: MCU.D3, TM1637.CLK
  N3: MCU.D5, Buzzer.pin1
  N4: MCU.D6, LASER_Fire.leg0
  N5: MCU.D7, Reset.leg0
  N6: MCU.D8, LASER_Diode.S
  N7: MCU.D9, Wireless_Communication.CS
  N8: MCU.D10, Wireless_Communication.CE
  N9: MCU.D11/MOSI, Wireless_Communication.MOSI
  N10: MCU.D12/MISO, Wireless_Communication.MISO
  N11: MCU.5V, 9V_Battery_(High_Current).V+
  N12: MCU.A1, R1.Pin_1
  3V3: MCU.3V3, Wireless_Communication.VCC
  N13: MCU.D13/SCK, Wireless_Communication.SCK
  GND: Reset.leg1, LASER_Fire.leg1, Buzzer.pin2, LASER_Diode.-, RED_LED.cathode, TM1637.VCC, 9V_Battery_(High_Current).V-
  N14: RED_LED.anode, R1.Pin_0

custom parts:
  KY-008 Laser Transmitter Module: KY-008 Laser Transmitter Module, emits a dot shaped red laser beam.
  TM1637: A 4 7-seg display
