# Fritzing sketch TARGET UNIT (saved by Fritzing 0.9.5d)
breadboards: 1

parts:
  MCU = Arduino Nano (Rev3.0)
  Reset = Round Pushbutton
  Buzzer = Piezo Speaker
  Green_LED = LED - 5mm [color="Green (560nm)" package="5 mm [THT]"]
  R1 = Resistor [tolerance=±5% resistance=220 package="2010 [SMD]"]
  TM1637 = TM1637
  Wireless_Communication = NRF24L01+ Breakout Board
  External_+5V_DC_supply = Power Jack [package=power_jack_pth_lock]
  R2 = Photocell (LDR) [package=THT]
  R3 = Resistor [tolerance=±5% resistance=10k package="0805 [SMD]"]
  RED_LED1 = LED - 5mm [color="Red (633nm)" package="5 mm [THT]"]
  R4 = Resistor [tolerance=±5% resistance=220 package="2010 [SMD]"]
  ON/OFF_Switch = Round Pushbutton

nets:
  N1: MCU.D2, TM1637.DIO
  N2: MCU.D3, TM1637.CLK
  N3: MCU.D4, Buzzer.pin1
  N4: MCU.D5, R1.Pin_1
  N5: MCU.D6, R2.pin_0, R3.Pin_0
  N6: MCU.D7, Reset.leg0
  N7: MCU.D9, Wireless_Communication.CS
  N8: MCU.D10, Wireless_Communication.CE
  N9: MCU.D11/MOSI, Wireless_Communication.MOSI
  N10: MCU.D12/MISO, Wireless_Communication.MISO
  N11: MCU.5V, R4.Pin_1, ON/OFF_Switch.leg1
  3V3: MCU.3V3, Wireless_Communication.VCC
  N12: MCU.D13/SCK, Wireless_Communication.SCK
  GND: Reset.leg1, Buzzer.pin2, Green_LED.cathode, TM1637.VCC, External_+5V_DC_supply.GNDBREAK, R2.pin_1, RED_LED1.cathode
  N13: Green_LED.anode, R1.Pin_0
  N14: External_+5V_DC_supply.PWR, ON/OFF_Switch.leg0
  5V: R3.Pin_1
  N15: RED_LED1.anode, R4.Pin_0

notes:
  LASER TARGET UNIT
  DRY Shooting Range V2.0

custom parts:
  TM1637: A 4 7-seg display
